# Fritzing sketch LCD_SM (saved by Fritzing 0.9.6b)

parts:
  U1 = keyestudio ESP32 plus development board [part_number=ESP32]
  IC1 = KS0061 [chip_label=?]

nets:
  GND: U1.GND, IC1.GND
  VCC: U1.5V, U1.VCC, IC1.VCC
  N1: U1.SDA, IC1.SDA
  N2: U1.SCL, IC1.SCL

custom parts:
  keyestudio ESP32 plus development board: keyestudio ESP32 plus STEM makers development board 2.4GHz dual-mode WiFi + bluetooth dual cores microcontroller
  KS0061: LCD 16x2 i2c
