# Fritzing sketch SM_thingspeak_conex (saved by Fritzing 0.9.6b)

parts:
  U1 = keyestudio ESP32 plus development board [part_number=ESP32]
  IC1 = KS0034 [chip_label=?]
  IC2 = KS0034 [chip_label=?]

nets:
  GND: U1.GND, IC1.GND, IC2.GND
  VCC: U1.5V, U1.VCC, IC1.VCC, IC2.VCC
  N1: U1.io25, IC1.S
  N2: U1.SDA, IC2.SDA
  N3: U1.SCL, IC2.SCL

custom parts:
  keyestudio ESP32 plus development board: keyestudio ESP32 plus STEM makers development board 2.4GHz dual-mode WiFi + bluetooth dual cores microcontroller
  KS0034: DHT-11
  KS0034: DHT-11
