# Fritzing sketch SM_thingspeak_servo (saved by Fritzing 0.9.6b)

parts:
  SERVO1 = Tower Pro SG90 servo [part_number=101246]
  U1 = keyestudio ESP32 plus development board [part_number=ESP32]
  IC1 = KS0029 [chip_label=?]

nets:
  N1: SERVO1.Signal, U1.io25
  VCC: SERVO1.+5V, U1.5V, U1.VCC, IC1.VCC
  GND: SERVO1.GND, U1.GND, IC1.GND
  N2: U1.io17, IC1.S

custom parts:
  Tower Pro SG90 servo: Original file by John De Cristofaro http://www.adafruit.com/products/1449 Adafruit Feedback Servo (Small) Edited by: e-radionica.com 28/9/2015
  keyestudio ESP32 plus development board: keyestudio ESP32 plus STEM makers development board 2.4GHz dual-mode WiFi + bluetooth dual cores microcontroller
  KS0029: Button
