# Fritzing sketch tira_led (saved by Fritzing 0.9.6b)
circuit board: 8.46667cm x 5.64444cm

parts:
  U1 = keyestudio ESP32 plus development board [part_number=ESP32]
  NEOPIXEL1 = Neopixel_Strip_Black_30_m

nets:
  N1: U1.GND, NEOPIXEL1.connector1
  5V: U1.5V, U1.VCC, NEOPIXEL1.connector3
  N2: U1.io12, NEOPIXEL1.connector2

custom parts:
  keyestudio ESP32 plus development board: keyestudio ESP32 plus STEM makers development board 2.4GHz dual-mode WiFi + bluetooth dual cores microcontroller
