# Fritzing sketch OLED (saved by Fritzing 0.9.6b)

parts:
  IC1 = ks0172 [chip_label=?]
  IC4 = KS0271_Front [chip_label=?]

nets:
  N1: IC1.SDA, IC4.SDA
  N2: IC1.SCL, IC4.SCL
  5V: IC1.5V, IC4.VCC
  GND: IC1.GND, IC4.GND

custom parts:
  ks0172: Arduino UNO R3 extra pins
  KS0271_Front: OLED i2c
