# Fritzing sketch SM_ultrasonidos (saved by Fritzing 0.9.6b)

parts:
  U1 = keyestudio ESP32 plus development board [part_number=ESP32]
  HC-SR04_Sensor_1 = HC-SR04 Ultrasonic Distance Sensor

nets:
  N1: U1.io2, HC-SR04_Sensor_1.TRIG
  GND: U1.GND, HC-SR04_Sensor_1.GND
  VCC: U1.5V, U1.VCC, U1.io34, HC-SR04_Sensor_1.VCC
  N2: U1.io4, HC-SR04_Sensor_1.ECHO

custom parts:
  keyestudio ESP32 plus development board: keyestudio ESP32 plus STEM makers development board 2.4GHz dual-mode WiFi + bluetooth dual cores microcontroller
