# Fritzing sketch LCD (saved by Fritzing 1.0.4)

parts:
  IC1 = ks0172 [chip_label=?]
  IC2 = KS0061 [chip_label=?]

nets:
  N1: IC1.SDA, IC2.SDA
  N2: IC1.SCL, IC2.SCL
  5V: IC1.5V, IC2.VCC
  GND: IC1.GND, IC2.GND

custom parts:
  ks0172: Arduino UNO R3 extra pins
  KS0061: LCD 16x2 i2c
